# Fritzing sketch gamepad (saved by Fritzing 0.9.0b)
breadboards: 1

parts:
  Part1 = Thumb Joystick
  Part2 = Arduino Nano (Rev3.0)
  S1 = Pushbutton [package="[THT]"]
  R1 = Resistor [tolerance=±5% resistance=1k package=THT]

nets:
  GND: Part1.GND, Part2.GND, R1.Pin_1
  N1: Part1.SEL, Part2.D5
  N2: Part1.HORZ, Part2.A0
  N3: Part1.VERT, Part2.A1
  VCC: Part1.VCC, Part2.5V
  N4: Part2.D2, S1.Pin_3, S1.Pin_4
  N5: Part2.D3, S1.Pin_1, S1.Pin_2, R1.Pin_0
